# Fritzing sketch Asistencia (saved by Fritzing 0.9.4)
breadboards: 1

parts:
  WeMos_D1_Mini2 = WeMos D1 Mini
  Componente1 = LilyPad Button Board
  BAT2 = Battery Holders [package=battcom_20mm_pth]

nets:
  N1: WeMos_D1_Mini2.3V3, BAT2.+
  N2: WeMos_D1_Mini2.G, Componente1.-, BAT2.-
  N3: WeMos_D1_Mini2.RST, Componente1.S
