# Fritzing sketch Optical dust sensor (saved by Fritzing 0.9.4)
breadboards: 1

parts:
  U1 = Sharp Dust Sensor [part_number=GP2Y1010AU0F]
  WeMos_D1_Mini1 = WeMos D1 Mini
  Componente2 = Lithium Ion Cylindrical Battery 3.7v 2200mAh [part_number=1781]
  C1 = Electrolytic Capacitor [capacitance=1µF package="100 mil [THT, electrolytic]"]
  R1 = Resistor [tolerance=±5% resistance=220 package="1206 [SMD]"]

nets:
  N1: U1.V-LED, C1.+, R1.Pin_1
  N2: U1.LED-GND, U1.S-GND, WeMos_D1_Mini1.G, Componente2.negative, C1.-
  N3: U1.LED, WeMos_D1_Mini1.D6
  N4: U1.Vo, WeMos_D1_Mini1.A0
  VCC: U1.VCC, WeMos_D1_Mini1.3V3, Componente2.positive, R1.Pin_0

custom parts:
  Sharp Dust Sensor: Sharp GP2Y1010AU0F Dust Sensor
  Lithium Ion Cylindrical Battery 3.7v 2200mAh: This lithium ion battery has a capacity of 2200mAh and a protection circuit that provides over-voltage, under-voltage and over-current protection. This cell can provide 2C of peak current (4400mA). Note that these batteries are not designed to sustain such high loads, we suggest keeping any constant current draw under about 0.5C (1 Amp).
