# Fritzing sketch RFID-RC522 (saved by Fritzing 0.9.4)
breadboards: 1

parts:
  Part2 = RFID-RC522-v2
  WeMos_D1_Mini1 = WeMos D1 Mini
  Componente1 = Lithium Ion Cylindrical Battery 3.7v 2200mAh [part_number=1781]

nets:
  N1: Part2.SDA, WeMos_D1_Mini1.D2
  N2: Part2.SCK, WeMos_D1_Mini1.D5
  N3: Part2.MOSI, WeMos_D1_Mini1.D7
  N4: Part2.MISO, WeMos_D1_Mini1.D6
  N5: Part2.GND, WeMos_D1_Mini1.G, Componente1.negative
  N6: Part2.RST, WeMos_D1_Mini1.D1
  3.3V: Part2.3.3V, WeMos_D1_Mini1.3V3, Componente1.positive

custom parts:
  RFID-RC522-v2: A simple China made RFID-RC522 Reader; do check the pin labels, as this is a MFRC522 based clone.
  Lithium Ion Cylindrical Battery 3.7v 2200mAh: This lithium ion battery has a capacity of 2200mAh and a protection circuit that provides over-voltage, under-voltage and over-current protection. This cell can provide 2C of peak current (4400mA). Note that these batteries are not designed to sustain such high loads, we suggest keeping any constant current draw under about 0.5C (1 Amp).
