# Fritzing sketch Sensor Pir (saved by Fritzing 0.9.4)
breadboards: 1

parts:
  WeMos_D1_Mini1 = WeMos D1 Mini
  Componente1 = Lithium Ion Cylindrical Battery 3.7v 2200mAh [part_number=1781]
  PIR1 = PIR sensor

nets:
  N1: WeMos_D1_Mini1.D3, PIR1.SIG
  N2: WeMos_D1_Mini1.G, Componente1.negative, PIR1.GND
  N3: Componente1.positive, PIR1.VDD

custom parts:
  Lithium Ion Cylindrical Battery 3.7v 2200mAh: This lithium ion battery has a capacity of 2200mAh and a protection circuit that provides over-voltage, under-voltage and over-current protection. This cell can provide 2C of peak current (4400mA). Note that these batteries are not designed to sustain such high loads, we suggest keeping any constant current draw under about 0.5C (1 Amp).
