# Fritzing sketch Sensor de Temperatura y Humedad (saved by Fritzing 0.9.4)
breadboards: 1

parts:
  M1 = BMP280
  WeMos_D1_Mini1 = WeMos D1 Mini
  Componente1 = Lithium Ion Cylindrical Battery 3.7v 2200mAh [part_number=1781]

nets:
  VIN: M1.VIN, WeMos_D1_Mini1.3V3, Componente1.positive
  N1: M1.GND, WeMos_D1_Mini1.G, Componente1.negative
  N2: M1.SCL, WeMos_D1_Mini1.D1
  N3: M1.SDA, WeMos_D1_Mini1.D2
  N4: WeMos_D1_Mini1.D0, WeMos_D1_Mini1.RST

custom parts:
  BMP280: Temperature Humidity Barometric presure Sensor, I2C
  Lithium Ion Cylindrical Battery 3.7v 2200mAh: This lithium ion battery has a capacity of 2200mAh and a protection circuit that provides over-voltage, under-voltage and over-current protection. This cell can provide 2C of peak current (4400mA). Note that these batteries are not designed to sustain such high loads, we suggest keeping any constant current draw under about 0.5C (1 Amp).
