# Fritzing sketch sensor magnetico (saved by Fritzing 0.9.4)
breadboards: 1

parts:
  WeMos_D1_Mini1 = WeMos D1 Mini
  Componente1 = Lithium Ion Cylindrical Battery 3.7v 2200mAh [part_number=1781]
  S1 = TILT-SWITCH-SW-200D [package=reed_switch_plastic]
  S2 = TILT-SWITCH-SW-200D [package=reed_switch_plastic]

nets:
  N1: WeMos_D1_Mini1.3V3, Componente1.positive
  N2: WeMos_D1_Mini1.D6, S1.2
  N3: WeMos_D1_Mini1.G, Componente1.negative, S1.1, S2.1
  N4: WeMos_D1_Mini1.RST, S2.2

custom parts:
  Lithium Ion Cylindrical Battery 3.7v 2200mAh: This lithium ion battery has a capacity of 2200mAh and a protection circuit that provides over-voltage, under-voltage and over-current protection. This cell can provide 2C of peak current (4400mA). Note that these batteries are not designed to sustain such high loads, we suggest keeping any constant current draw under about 0.5C (1 Amp).
